# Fritzing sketch Binary Counter (saved by Fritzing 0.9.2b)
breadboards: 2

parts:
  LED1 = LED - 5mm [color="Red (633nm)" package="5 mm [THT]"]
  LED2 = LED - 5mm [color="Red (633nm)" package="5 mm [THT]"]
  LED3 = LED - 5mm [color="Yellow (585nm)" package="5 mm [THT]"]
  LED4 = LED - 5mm [color="Yellow (585nm)" package="5 mm [THT]"]
  LED5 = LED - 5mm [color="Yellow (585nm)" package="5 mm [THT]"]
  LED6 = LED - 5mm [color="Yellow (585nm)" package="5 mm [THT]"]
  LED7 = LED - 5mm [color="Yellow (585nm)" package="5 mm [THT]"]
  LED8 = LED - 5mm [color="Yellow (585nm)" package="5 mm [THT]"]
  LED9 = LED - 5mm [color="Green (555nm)" package="5 mm [THT]"]
  LED10 = LED - 5mm [color="Green (555nm)" package="5 mm [THT]"]
  LED11 = LED - 5mm [color="Green (555nm)" package="5 mm [THT]"]
  LED12 = LED - 5mm [color="Green (555nm)" package="5 mm [THT]"]
  LED13 = LED - 5mm [color="Green (555nm)" package="5 mm [THT]"]
  LED14 = LED - 5mm [color="Green (555nm)" package="5 mm [THT]"]
  LED15 = LED - 5mm [color="Blue (505nm)" package="5 mm [THT]"]
  LED16 = LED - 5mm [color="Blue (505nm)" package="5 mm [THT]"]
  LED17 = LED - 5mm [color="Blue (505nm)" package="5 mm [THT]"]
  R2 = Resistor [tolerance=±1% resistance=330 package=THT]
  R3 = Resistor [tolerance=±1% resistance=330 package=THT]
  R4 = Resistor [tolerance=±1% resistance=330 package=THT]
  R5 = Resistor [tolerance=±1% resistance=330 package=THT]
  R6 = Resistor [tolerance=±1% resistance=330 package=THT]
  R7 = Resistor [tolerance=±1% resistance=330 package=THT]
  R8 = Resistor [tolerance=±1% resistance=330 package=THT]
  R9 = Resistor [tolerance=±1% resistance=330 package=THT]
  R10 = Resistor [tolerance=±1% resistance=330 package=THT]
  R11 = Resistor [tolerance=±1% resistance=330 package=THT]
  R12 = Resistor [tolerance=±1% resistance=330 package=THT]
  R13 = Resistor [tolerance=±1% resistance=330 package=THT]
  R14 = Resistor [tolerance=±1% resistance=330 package=THT]
  R15 = Resistor [tolerance=±1% resistance=330 package=THT]
  R16 = Resistor [tolerance=±1% resistance=330 package=THT]
  R17 = Resistor [tolerance=±1% resistance=330 package=THT]
  R18 = Resistor [tolerance=±1% resistance=330 package=THT]
  J1 = Cobbler Plus  # not connected
  S1 = Pushbutton [package="[THT]"]
  S2 = Pushbutton [package="[THT]"]
  S3 = Pushbutton [package="[THT]"]
  S4 = Pushbutton [package="[THT]"]

nets:
  N1: LED1.cathode, LED2.cathode, LED3.cathode, LED4.cathode, LED5.cathode, LED6.cathode, LED7.cathode, LED8.cathode, LED9.cathode, LED10.cathode, LED11.cathode, LED12.cathode, LED13.cathode, LED14.cathode, LED15.cathode, LED16.cathode, LED17.cathode, S1.Pin_1, S1.Pin_2, S2.Pin_1, S2.Pin_2, S3.Pin_1, S3.Pin_2, S4.Pin_1, S4.Pin_2
  N2: LED1.anode, R3.Pin_1
  N3: LED2.anode, R2.Pin_1
  N4: LED3.anode, R8.Pin_1
  N5: LED4.anode, R9.Pin_1
  N6: LED5.anode, R7.Pin_1
  N7: LED6.anode, R11.Pin_1
  N8: LED7.anode, R12.Pin_1
  N9: LED8.anode, R10.Pin_1
  N10: LED9.anode, R14.Pin_1
  N11: LED10.anode, R15.Pin_1
  N12: LED11.anode, R13.Pin_1
  N13: LED12.anode, R17.Pin_1
  N14: LED13.anode, R18.Pin_1
  N15: LED14.anode, R16.Pin_1
  N16: LED15.anode, R5.Pin_1
  N17: LED16.anode, R4.Pin_1
  N18: LED17.anode, R6.Pin_1
  N19: S1.Pin_3, S1.Pin_4
  N20: S2.Pin_3, S2.Pin_4
  N21: S3.Pin_3, S3.Pin_4
  N22: S4.Pin_3, S4.Pin_4

custom parts:
  Cobbler Plus: The Cobbler Plus is an add on prototyping board from Adafruit specifically designed for the Raspberry Pi B+ that can break out all those tasty power, GPIO, I2C and SPI pins from the 40-pin header onto a solderless breadboard. This set will make "cobbling together" prototypes with the Pi super easy. The Cobbler Plus can plug into any solderless breadboard.
