# Fritzing sketch LED (saved by Fritzing 0.9.2b)

parts:
  Raspberry_Pi1 = Raspberry Pi B+
  LED1 = smd LED [color="Red (633nm)" package="1206 [SMD]"]
  R1 = Resistor [tolerance=±5% resistance=68 package="0603 [SMD]"]

nets:
  N1: Raspberry_Pi1.GPIO18, R1.Pin_0
  N2: Raspberry_Pi1.GND, LED1.cathode
  N3: LED1.anode, R1.Pin_1

notes:
  Parts:
  Raspberry Pi B+
  Red 5mm LED
  68Ω Resistor
